// Logisim project Digital Interval Timer.circ as structural Verilog: 1 circuit, main circuit main
module main (
  input  [3:0] in_1,
  input  [3:0] in_2,
  input  [3:0] Work,
  input  [3:0] in_4,
  input  [3:0] Rest,
  input  [3:0] in_6,
  input  [3:0] Work_2,
  input  [3:0] Rest_2,
  input  [3:0] Work_3,
  input  [3:0] Rest_3,
  input  E,
  input  [3:0] Work_4,
  input  [3:0] Rest_4
);

  wire and_1_out, clock_1_out, clock_2_out, comparator_1_eq, comparator_2_eq, comparator_3_eq,
       comparator_4_eq, d_ff_1_q, MinOnes_carry, nand_1_out, nand_2_out, nand_3_out, nand_4_out, not_1_out,
       not_2_out, R_out, S_out, SecOnes_carry, SecTens_carry;
  wire [3:0] MinOnes_q, MinTens_q, multiplexer_1_out, multiplexer_2_out, multiplexer_3_out,
       multiplexer_4_out, SecOnes_q, SecTens_q;

  Button S (.out(S_out));
  Button R (.out(R_out));
  not not_1 (not_1_out, S_out);
  not not_2 (not_2_out, R_out);
  Counter #(.width(4), .max('h3), .trigger("falling")) MinTens (
    .load(1'b1), .D(multiplexer_1_out), .count(nand_3_out), .Q(MinTens_q), .clk(MinOnes_carry), .clr(R_out));  // open: carry
  Counter #(.width(4), .max('h9), .trigger("falling")) MinOnes (
    .load(1'b1), .D(multiplexer_2_out), .count(nand_3_out), .Q(MinOnes_q), .carry(MinOnes_carry),
    .clk(SecTens_carry), .clr(R_out));
  nand nand_1 (nand_1_out, not_1_out, E);
  nand nand_2 (nand_2_out, E, not_2_out);
  Hex_Digit_Display hex_digit_display_1 (.value(MinTens_q));  // open: dp
  Hex_Digit_Display hex_digit_display_2 (.value(MinOnes_q));  // open: dp
  Comparator #(.width(4)) comparator_1 (.a(MinTens_q), .b(in_1), .eq(comparator_1_eq));  // open: gt, lt
  Comparator #(.width(4)) comparator_2 (.a(MinOnes_q), .b(in_6), .eq(comparator_2_eq));  // open: gt, lt
  nand nand_3 (nand_3_out, nand_4_out, nand_1_out);
  nand nand_4 (nand_4_out, nand_3_out, nand_2_out);
  Counter #(.width(4), .max('h5), .trigger("falling")) SecTens (
    .load(1'b1), .D(multiplexer_3_out), .count(nand_3_out), .Q(SecTens_q), .carry(SecTens_carry),
    .clk(SecOnes_carry), .clr(R_out));
  Counter #(.width(4), .max('h9), .trigger("falling")) SecOnes (
    .load(1'b1), .D(multiplexer_4_out), .count(nand_3_out), .Q(SecOnes_q), .carry(SecOnes_carry),
    .clk(clock_1_out), .clr(R_out));
  Clock clock_1 (.out(clock_1_out));
  Hex_Digit_Display hex_digit_display_3 (.value(SecOnes_q));  // open: dp
  Hex_Digit_Display hex_digit_display_4 (.value(SecTens_q));  // open: dp
  Comparator #(.width(4)) comparator_3 (.a(SecTens_q), .b(in_2), .eq(comparator_3_eq));  // open: gt, lt
  Comparator #(.width(4)) comparator_4 (.a(SecOnes_q), .b(in_4), .eq(comparator_4_eq));  // open: gt, lt
  Clock clock_2 (.out(clock_2_out));
  and and_1 (and_1_out, comparator_3_eq, comparator_4_eq, comparator_2_eq, comparator_1_eq);
  D_Flip_Flop d_ff_1 (
    .clk(clock_2_out), .D(and_1_out), .Q(d_ff_1_q), .preset(1'b1), .en(1'b1), .reset(1'b1));  // open: Qn
  Multiplexer #(.width(4)) multiplexer_1 (.in0(Work), .in1(Rest), .out(multiplexer_1_out), .sel(d_ff_1_q), .en(1'b1));
  Multiplexer #(.width(4)) multiplexer_2 (
    .in0(Work_2), .in1(Rest_2), .out(multiplexer_2_out), .sel(d_ff_1_q), .en(1'b1));
  Multiplexer #(.width(4)) multiplexer_3 (
    .in0(Work_3), .in1(Rest_3), .out(multiplexer_3_out), .sel(d_ff_1_q), .en(1'b1));
  Multiplexer #(.width(4)) multiplexer_4 (
    .in0(Work_4), .in1(Rest_4), .out(multiplexer_4_out), .sel(d_ff_1_q), .en(1'b1));

  // Notes on the sheet:
  //   When S=0 and R=1 "Reset | Q=0
  //   When S=1 and R=0 "Set" | Q=1
  //   Q
  //   Q'
  //   work timer done
  //   minTens
  //   minUnits
  //   secTens
  //   secUnits
endmodule
